# Fritzing sketch finalproj (saved by Fritzing 0.9.9b)
breadboards: 1

parts:
  Pro_Micro1 = SparkFun Pro Micro
  Mod1 = Microbit
  M1 = MAX30102
  Part1 = Adafruit DRV2605L [part_number="Adafruit #2305"]
  U1 = Vibration Motor- ROB-08449 [package=vibe-motor-10mm]
  R1 = Resistor [tolerance=±5% power=0.25 resistance=10k package=THT]
  R3 = Resistor [tolerance=±5% power=0.25 resistance=10k package=THT]
  VCC1 = Battery

nets:
  N1: Pro_Micro1.TX0, Mod1.P2, Mod1.P13
  GND: Pro_Micro1.GND, Mod1.GND, Mod1.Bat_-, M1.GND, Part1.GND, VCC1.-
  N2: Pro_Micro1.2, M1.SDA
  N3: Pro_Micro1.3, M1.SCL
  VIN: Pro_Micro1.VCC, M1.VIN, Part1.VIN, R1.Pin_1, R3.Pin_1
  N4: Mod1.P0, Mod1.P4, Part1.SCL, R1.Pin_0
  N5: Mod1.P1, Mod1.P8, Part1.SDA, R3.Pin_0
  N6: Mod1.Bat_+, VCC1.+
  N7: Part1.OUT+, U1.-
  N8: Part1.OUT-, U1.+

custom parts:
  SparkFun Pro Micro: The Pro Micro is similar to the Pro Mini except with an ATmega32U4 on board. The USB transceiver inside the 32U4 allows us to add USB connectivity on-board and do away with bulky external USB interface. Based on: https://github.com/unorthodox-engineers/unorthodox-arduino/blob/master/Unorthodox/fritzing/parts/Pro%20Micro.fzpz
  Microbit: BBC Microbit Fritzing part. May 2019 expanded to include schematic and pcb views as well as breadboard. PCB view assumes an Adafruit PRODUCT ID: 3342 2x40 Right Angle through hole edge connector (although others will probably work as well). The pcb svg is custom (see forum article http://forum.fritzing.org/t/making-edge-connectors-and-both-side-smd-parts/7287 for an explaination if you need to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
  MAX30102: Oximeter module using the MAX30102 chip. You may wish to read (and check your module) this post on power problems with these modules: https://reedpaper.wordpress.com/2018/08/22/pulse-oximeter-max30100-max30102-how-to-fix-wrong-board/ . As usual, if you want the mounting holes in pcb, you need to drag a hole over the pad in silkscreen to actually drill the hole (by default they are not drilled)
  Adafruit DRV2605L: The DRV2605 from TI is a fancy little motor driver. Rather than controlling a stepper motor or DC motor, its designed specifically for controlling haptic motors - buzzers and vibration motors. Normally one would just turn those kinds of motors on and off, but this driver has the ability to have various effects when driving a vibe motor. For example, ramping the vibration level up and down,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
